// Logisim project current_cpu_design.circ as structural Verilog: 7 circuits, main circuit reg8
module reg8 (
  input  Write,
  input  [2:0] Write_register,
  input  [15:0] write_data,
  input  clock,
  input  [2:0] read_register2,
  input  [2:0] read_register1,
  input  reset,
  output [15:0] read_data1,
  output [15:0] read_data2
);

  wire and_1_out, and_2_out, and_3_out, and_4_out, and_5_out, and_6_out, and_7_out, and_8_out,
       decoder_1_out0, decoder_1_out1, decoder_1_out2, decoder_1_out3, decoder_1_out4, decoder_1_out5,
       decoder_1_out6, decoder_1_out7;
  wire [15:0] register_1_q, register_2_q, register_3_q, register_4_q, register_5_q, register_6_q,
       register_7_q, register_8_q;

  Decoder #(.select(3), .enable("false")) decoder_1 (
    .out0(decoder_1_out0), .out1(decoder_1_out1), .out2(decoder_1_out2), .out3(decoder_1_out3),
    .out4(decoder_1_out4), .out5(decoder_1_out5), .out6(decoder_1_out6), .out7(decoder_1_out7),
    .sel(Write_register));
  and and_1 (and_1_out, Write, decoder_1_out0);
  and and_2 (and_2_out, Write, decoder_1_out1);
  and and_3 (and_3_out, Write, decoder_1_out2);
  and and_4 (and_4_out, Write, decoder_1_out3);
  and and_5 (and_5_out, Write, decoder_1_out4);
  and and_6 (and_6_out, Write, decoder_1_out5);
  and and_7 (and_7_out, Write, decoder_1_out6);
  and and_8 (and_8_out, Write, decoder_1_out7);
  Register #(.width(16)) register_1 (.D(write_data), .en(and_1_out), .Q(register_1_q), .clk(clock), .clr(reset));
  Register #(.width(16)) register_2 (.D(write_data), .en(and_2_out), .Q(register_2_q), .clk(clock), .clr(reset));
  Register #(.width(16)) register_3 (.D(write_data), .en(and_3_out), .Q(register_3_q), .clk(clock), .clr(reset));
  Register #(.width(16)) register_4 (.D(write_data), .en(and_4_out), .Q(register_4_q), .clk(clock), .clr(reset));
  Register #(.width(16)) register_5 (.D(write_data), .en(and_5_out), .Q(register_5_q), .clk(clock), .clr(reset));
  Register #(.width(16)) register_6 (.D(write_data), .en(and_6_out), .Q(register_6_q), .clk(clock), .clr(reset));
  Register #(.width(16)) register_7 (.D(write_data), .en(and_7_out), .Q(register_7_q), .clk(clock), .clr(reset));
  Register #(.width(16)) register_8 (.D(write_data), .en(and_8_out), .Q(register_8_q), .clk(clock), .clr(reset));
  Multiplexer #(.select(3), .width(16), .enable("false")) multiplexer_1 (
    .in0(register_1_q), .in1(register_2_q), .in2(register_3_q), .in3(register_4_q), .in4(register_5_q),
    .in5(register_6_q), .in6(register_7_q), .in7(register_8_q), .out(read_data1), .sel(read_register1));
  Multiplexer #(.select(3), .width(16), .enable("false")) multiplexer_2 (
    .in0(register_1_q), .in1(register_2_q), .in2(register_3_q), .in3(register_4_q), .in4(register_5_q),
    .in5(register_6_q), .in6(register_7_q), .in7(register_8_q), .out(read_data2), .sel(read_register2));
endmodule

module ALU_NEW (
  input  [15:0] d1,
  input  [15:0] d2,
  input  [1:0] alusignal,
  output bltsignal,
  output [15:0] \output 
);

  wire [15:0] adder_1_out, and_1_out, or_1_out;

  Comparator #(.width(16), .mode("unsigned")) comparator_1 (.a(d1), .b(d2), .lt(bltsignal));  // open: gt, eq
  Adder #(.width(16)) adder_1 (.a(d1), .b(d2), .out(adder_1_out));  // open: cin, cout
  assign and_1_out = d1 & d2;  // AND_Gate and_1, 16 bits wide
  assign or_1_out = d1 | d2;  // OR_Gate or_1, 16 bits wide
  Multiplexer #(.select(2), .width(16)) multiplexer_1 (
    .in0(adder_1_out), .in1(and_1_out), .in2(or_1_out), .out(\output ), .sel(alusignal), .en(1'b1));  // open: in3
endmodule

module Mycontrol (
  input  x4,
  input  x3,
  input  x2,
  input  x1,
  output RegDst,
  output ALUSrc,
  output memtoreg,
  output RegWrite,
  output MemRead,
  output MemWrite,
  output Branch,
  output Jump,
  output ALU01,
  output ALU02,
  output raread,
  output rawrite,
  output halt,
  output li
);

  wire and_1_out, and_2_out, and_3_out, and_4_out, and_5_out, and_6_out, and_8_out, and_9_out, and_10_out,
       and_11_out, and_12_out, and_16_out, and_17_out, and_18_out, and_19_out, and_20_out, and_21_out,
       and_22_out, and_23_out, and_24_out, and_25_out, not_1_out, not_2_out, not_3_out, not_4_out, not_5_out,
       not_6_out, not_7_out, not_8_out, not_9_out, not_10_out, not_11_out, not_12_out, not_13_out,
       not_14_out, not_15_out, not_16_out, not_17_out, not_18_out, not_19_out, not_20_out, not_21_out,
       not_22_out, not_23_out, not_24_out, not_25_out, not_26_out, not_27_out, not_28_out, not_29_out,
       not_30_out, not_31_out, not_32_out, not_33_out, not_34_out, not_35_out, not_36_out, not_37_out,
       not_38_out, not_39_out, not_40_out, not_41_out, not_42_out, not_43_out, not_44_out, not_45_out,
       not_46_out, not_47_out, not_48_out, not_49_out, not_50_out, not_51_out, or_1_out;

  not not_1 (not_1_out, x4);
  not not_2 (not_2_out, x3);
  not not_3 (not_3_out, x2);
  not not_4 (not_4_out, x1);
  not not_5 (not_5_out, x4);
  not not_6 (not_6_out, x2);
  not not_7 (not_7_out, x4);
  not not_8 (not_8_out, x1);
  not not_9 (not_9_out, x4);
  not not_10 (not_10_out, x3);
  or or_1 (or_1_out, x2, x1);
  not not_11 (not_11_out, x3);
  not not_12 (not_12_out, x2);
  not not_13 (not_13_out, x3);
  not not_14 (not_14_out, x2);
  not not_15 (not_15_out, x1);
  not not_16 (not_16_out, x4);
  not not_17 (not_17_out, x3);
  not not_18 (not_18_out, x4);
  not not_19 (not_19_out, x1);
  not not_20 (not_20_out, x2);
  not not_21 (not_21_out, x3);
  not not_22 (not_22_out, x2);
  not not_23 (not_23_out, x1);
  not not_24 (not_24_out, x3);
  not not_25 (not_25_out, x2);
  not not_26 (not_26_out, x1);
  not not_27 (not_27_out, x3);
  not not_28 (not_28_out, x2);
  not not_29 (not_29_out, x2);
  not not_30 (not_30_out, x1);
  not not_31 (not_31_out, x4);
  not not_32 (not_32_out, x3);
  not not_33 (not_33_out, x4);
  not not_34 (not_34_out, x2);
  not not_35 (not_35_out, x4);
  not not_36 (not_36_out, x3);
  not not_37 (not_37_out, x4);
  not not_38 (not_38_out, x1);
  not not_39 (not_39_out, x4);
  not not_40 (not_40_out, x3);
  not not_41 (not_41_out, x2);
  not not_42 (not_42_out, x4);
  not not_43 (not_43_out, x3);
  not not_44 (not_44_out, x4);
  not not_45 (not_45_out, x1);
  not not_46 (not_46_out, x3);
  not not_47 (not_47_out, x2);
  not not_48 (not_48_out, x4);
  not not_49 (not_49_out, x3);
  not not_50 (not_50_out, x1);
  not not_51 (not_51_out, x2);
  and and_1 (and_1_out, not_1_out, not_2_out, not_3_out, not_4_out);
  and and_2 (and_2_out, not_5_out, x3, not_6_out, x1);
  and and_3 (and_3_out, not_7_out, x3, x2, not_8_out);
  and and_4 (and_4_out, not_9_out, not_10_out, or_1_out);
  and and_5 (and_5_out, x4, x3, x1);
  and and_6 (and_6_out, x4, not_11_out, not_12_out);
  and and_7 (memtoreg, x4, not_13_out, not_14_out, not_15_out);
  and and_8 (and_8_out, not_16_out, not_17_out);
  and and_9 (and_9_out, not_18_out, x2, not_19_out);
  and and_10 (and_10_out, x3, not_20_out, x1);
  and and_11 (and_11_out, x4, x3, x1);
  and and_12 (and_12_out, not_21_out, not_22_out, not_23_out);
  and and_13 (MemRead, x4, not_24_out, not_25_out, not_26_out);
  and and_14 (MemWrite, x4, not_27_out, not_28_out, x1);
  and and_15 (Branch, x3, not_29_out, not_30_out);
  and and_16 (and_16_out, not_31_out, x3, x2, x1);
  and and_17 (and_17_out, x4, not_32_out, x2);
  and and_18 (and_18_out, not_33_out, x3, not_34_out, x1);
  and and_19 (and_19_out, not_35_out, not_36_out, x2);
  and and_20 (and_20_out, not_37_out, x2, not_38_out);
  and and_21 (and_21_out, not_39_out, not_40_out, not_41_out);
  and and_22 (and_22_out, not_42_out, not_43_out, x1);
  and and_23 (and_23_out, not_44_out, x3, x2, not_45_out);
  and and_24 (and_24_out, x4, x3, x1);
  and and_25 (and_25_out, x4, not_46_out, not_47_out);
  and and_26 (raread, not_48_out, x3, x2, x1);
  and and_27 (rawrite, x4, not_49_out, x2, x1);
  and and_28 (halt, x4, x3, x2, not_50_out);
  and and_29 (li, x4, x3, not_51_out, x1);
  or or_2 (RegDst, and_1_out, and_2_out, and_3_out);
  or or_3 (ALUSrc, and_4_out, and_5_out, and_6_out);
  or or_4 (RegWrite, and_8_out, and_9_out, and_10_out, and_11_out, and_12_out);
  or or_5 (Jump, and_16_out, and_17_out);
  or or_6 (ALU01, and_18_out, and_19_out, and_20_out);
  or or_7 (ALU02, and_21_out, and_22_out, and_23_out, and_24_out, and_25_out);

  // Notes on the sheet:
  //   read from bottom to top
endmodule

module Control (
  input  [3:0] opcode__x4_x3_x2_x1,
  output RegDst,
  output ALUSrc,
  output Memtoreg,
  output RegWrite,
  output MemRead,
  output MemWrite,
  output Branch,
  output Jump,
  output [1:0] ALUOp,
  output raread,
  output halt,
  output rawrite,
  output li
);

  Mycontrol mycontrol_1 (
    .x4(opcode__x4_x3_x2_x1[3]), .x3(opcode__x4_x3_x2_x1[2]), .x2(opcode__x4_x3_x2_x1[1]),
    .x1(opcode__x4_x3_x2_x1[0]), .RegDst(RegDst), .ALUSrc(ALUSrc), .memtoreg(Memtoreg), .RegWrite(RegWrite),
    .MemRead(MemRead), .MemWrite(MemWrite), .Branch(Branch), .Jump(Jump), .ALU01(ALUOp[0]), .ALU02(ALUOp[1]),
    .raread(raread), .rawrite(rawrite), .halt(halt), .li(li));
endmodule

module _16_bit_cpu (
);

  wire alu_new_1_bltsignal, and_1_out, clock, clock_1_out, control_1_alusrc, control_1_branch,
       control_1_jump, control_1_li, control_1_memread, control_1_memtoreg, control_1_memwrite,
       control_1_regdst, halt, or_1_out, reset, rread, rwrite, W;
  wire [1:0] control_1_aluop;
  wire [2:0] w_t;
  wire [15:0] adder_1_out, adder_2_out, alu_new_1_output, bit_extender_1_out, jump_minus_64_1_out_2,
       multiplexer_1_out, multiplexer_2_out, multiplexer_5_out, multiplexer_6_out, multiplexer_7_out,
       multiplexer_8_out, PC_q, ra_register_1_data1, ram_1_data, reg8_1_read_data1, reg8_1_read_data2,
       rom_1_data, subtractor_1_out;

  Multiplexer #(.width(16), .enable("false")) multiplexer_1 (
    .in0(adder_1_out), .in1(adder_2_out), .out(multiplexer_1_out), .sel(or_1_out));
  Clock clock_1 (.out(clock_1_out));
  Multiplexer #(.width(16), .enable("false")) multiplexer_2 (
    .in0(multiplexer_1_out), .in1(multiplexer_5_out), .out(multiplexer_2_out), .sel(rread));
  Multiplexer #(.enable("false")) multiplexer_3 (.in0(clock_1_out), .in1(1'b0), .out(clock), .sel(halt));
  Button button_1 (.out(reset));
  Register #(.width(16)) PC (.D(jump_minus_64_1_out_2), .Q(PC_q), .clk(clock), .clr(reset));  // open: en
  jump_minus_64 jump_minus_64_1 (.in_1(multiplexer_2_out), .out_2(jump_minus_64_1_out_2));
  Adder #(.width(16)) adder_1 (.a(PC_q), .b(16'h1), .out(adder_1_out));  // open: cin, cout
  ROM #(.addrWidth(16), .dataWidth(16)) rom_1 (.addr(PC_q), .data(rom_1_data));  // open: sel
  assign bit_extender_1_out = {{10{1'b0}}, {rom_1_data[11:9], rom_1_data[2:0]}};  // Bit_Extender bit_extender_1
  ra_register ra_register_1 (
    .Write(rwrite), .in_2(adder_1_out), .clock(clock), .reset(reset), .Read(rread),
    .Data1(ra_register_1_data1));
  Control control_1 (
    .opcode__x4_x3_x2_x1(rom_1_data[15:12]), .RegDst(control_1_regdst), .ALUSrc(control_1_alusrc),
    .Memtoreg(control_1_memtoreg), .RegWrite(W), .MemRead(control_1_memread), .MemWrite(control_1_memwrite),
    .Branch(control_1_branch), .Jump(control_1_jump), .ALUOp(control_1_aluop), .raread(rread), .halt(halt),
    .rawrite(rwrite), .li(control_1_li));
  Multiplexer #(.width(3), .enable("false")) multiplexer_4 (
    .in0(rom_1_data[8:6]), .in1(rom_1_data[2:0]), .out(w_t), .sel(control_1_regdst));
  Multiplexer #(.width(16), .enable("false")) multiplexer_5 (
    .in0({16{1'b0}}), .in1(ra_register_1_data1), .out(multiplexer_5_out), .sel(rread));
  reg8 reg8_1 (
    .Write(W), .Write_register(w_t), .write_data(multiplexer_8_out), .clock(clock), .reset(reset),
    .read_register2(rom_1_data[8:6]), .read_register1(rom_1_data[5:3]), .read_data1(reg8_1_read_data1),
    .read_data2(reg8_1_read_data2));
  and and_1 (and_1_out, control_1_branch, alu_new_1_bltsignal);
  or or_1 (or_1_out, and_1_out, control_1_jump);
  Multiplexer #(.width(16), .enable("false")) multiplexer_6 (
    .in0(reg8_1_read_data2), .in1(bit_extender_1_out), .out(multiplexer_6_out), .sel(control_1_alusrc));
  Multiplexer #(.width(16), .enable("false")) multiplexer_7 (
    .in0(reg8_1_read_data1), .in1({16{1'b0}}), .out(multiplexer_7_out), .sel(control_1_li));
  Subtractor #(.width(16)) subtractor_1 (.a(bit_extender_1_out), .b(16'h1), .out(subtractor_1_out));  // open: bin, bout
  ALU_NEW alu_new_1 (
    .d1(multiplexer_7_out), .d2(multiplexer_6_out), .alusignal(control_1_aluop),
    .bltsignal(alu_new_1_bltsignal), .\output (alu_new_1_output));
  Adder #(.width(16)) adder_2 (.a(adder_1_out), .b(subtractor_1_out), .out(adder_2_out));  // open: cin, cout
  RAM #(.addrWidth(16), .dataWidth(16), .bus("separate")) ram_1 (
    .addr(reg8_1_read_data2), .din(alu_new_1_output), .data(ram_1_data), .str(control_1_memwrite),
    .clk(clock), .ld(control_1_memread), .clr(reset));  // open: sel
  Multiplexer #(.width(16), .enable("false")) multiplexer_8 (
    .in0(alu_new_1_output), .in1(ram_1_data), .out(multiplexer_8_out), .sel(control_1_memtoreg));

  // Notes on the sheet:
  //   contents of rom_1 (hex, n*v repeats v):
  //   d041 d082 8a 9010
endmodule

module ra_register (
  input  Write,
  input  [15:0] in_2,
  input  Read,
  input  clock,
  input  reset,
  output [15:0] Data1
);

  wire [15:0] register_1_q;

  Register #(.width(16)) register_1 (.D(in_2), .en(Write), .Q(register_1_q), .clk(clock), .clr(reset));
  assign Data1 = Read ? register_1_q : 16'bz;  // Controlled_Buffer controlled_buffer_1
endmodule

module jump_minus_64 (
  input  [15:0] in_1,
  output [15:0] out_2
);

  wire comparator_1_gt;
  wire [15:0] subtractor_1_out;

  Subtractor #(.width(16)) subtractor_1 (.a(in_1), .b(16'h40), .out(subtractor_1_out));  // open: bin, bout
  Comparator #(.width(16), .mode("unsigned")) comparator_1 (
    .a(in_1), .b(16'h40), .gt(comparator_1_gt));  // open: eq, lt
  Multiplexer #(.width(16), .enable("false")) multiplexer_1 (
    .in0(in_1), .in1(subtractor_1_out), .out(out_2), .sel(comparator_1_gt));
endmodule
