// Logisim project current_cpu_design_last.circ as structural Verilog: 15 circuits, main circuit reg8
module main_16_bit_cpu (
);

  wire alu_1_blesignal, alu_1_bne, ALUSrc, and_1_out, and_2_out, call, clock, clock_1_out, control_1_jump,
       control_1_li, control_1_memread, control_1_memtoreg, control_1_memwrite, control_1_regdst, halt,
       or_1_out, reset, ret, rread, rwrite, W;
  wire [1:0] control_1_aluop, control_1_branch;
  wire [2:0] readReg1, readReg1L, readReg2, w_t;
  wire [15:0] adder_1_out, adder_2_out, alu_1_output, bit_extender_1_out, jump_minus_64_1_out_2,
       multiplexer_1_out, multiplexer_2_out, multiplexer_6_out, multiplexer_7_out, multiplexer_8_out, PC_q,
       ra_register_1_data1, ram_1_data, reg8_1_read_data1, reg8_1_read_data2, rom_1_data, subtractor_1_out;

  Multiplexer #(.width(16), .enable("false")) multiplexer_1 (
    .in0(adder_1_out), .in1(adder_2_out), .out(multiplexer_1_out), .sel(or_1_out));
  Multiplexer #(.width(16), .enable("false")) multiplexer_2 (
    .in0(multiplexer_1_out), .in1(ra_register_1_data1), .out(multiplexer_2_out), .sel(rread));
  Clock clock_1 (.out(clock_1_out));
  jump_minus_64 jump_minus_64_1 (.in_1(multiplexer_2_out), .out_2(jump_minus_64_1_out_2));
  Multiplexer #(.enable("false")) multiplexer_3 (.in0(clock_1_out), .in1(1'b0), .out(clock), .sel(halt));
  Button button_1 (.out(reset));
  Register #(.width(16)) PC (.D(jump_minus_64_1_out_2), .Q(PC_q), .clk(clock), .clr(reset));  // open: en
  Adder #(.width(16)) adder_1 (.a(PC_q), .b(16'h1), .out(adder_1_out));  // open: cin, cout
  ROM #(.addrWidth(16), .dataWidth(16)) rom_1 (
    .addr(PC_q), .data({rom_1_data[15:9], readReg2, readReg1, rom_1_data[2:0]}));  // open: sel
  Control control_1 (
    .opcode__x4_x3_x2_x1(rom_1_data[15:12]), .RegDst(control_1_regdst), .ALUSrc(ALUSrc),
    .Memtoreg(control_1_memtoreg), .RegWrite(W), .MemRead(control_1_memread), .MemWrite(control_1_memwrite),
    .Branch(control_1_branch), .Jump(control_1_jump), .ALUOp(control_1_aluop), .raread(rread), .halt(halt),
    .rawrite(rwrite), .li(control_1_li), .call(call), .ret(ret));
  assign bit_extender_1_out = {{10{1'b0}}, {rom_1_data[11:9], rom_1_data[2:0]}};  // Bit_Extender bit_extender_1
  ra_register ra_register_1 (
    .Write(rwrite), .in_2(adder_1_out), .clock(clock), .reset(reset), .Read(rread),
    .Data1(ra_register_1_data1));
  Multiplexer #(.width(3), .enable("false")) multiplexer_4 (
    .in0(readReg1), .in1(rom_1_data[2:0]), .out(w_t), .sel(control_1_regdst));
  reg8 reg8_1 (
    .Write(W), .Write_register(w_t), .write_data(multiplexer_8_out), .clock(clock), .reset(reset),
    .read_register2(readReg2), .read_register1(readReg1L), .read_data1(reg8_1_read_data1),
    .read_data2(reg8_1_read_data2));
  Multiplexer #(.width(3), .enable("false")) multiplexer_5 (
    .in0(readReg1), .in1(readReg2), .out(readReg1L), .sel(ALUSrc));
  and and_1 (and_1_out, control_1_branch[0], alu_1_blesignal);
  and and_2 (and_2_out, alu_1_bne, control_1_branch[1]);
  or or_1 (or_1_out, and_1_out, and_2_out, control_1_jump);
  Multiplexer #(.width(16), .enable("false")) multiplexer_6 (
    .in0(reg8_1_read_data2), .in1(bit_extender_1_out), .out(multiplexer_6_out), .sel(ALUSrc));
  Multiplexer #(.width(16), .enable("false")) multiplexer_7 (
    .in0(reg8_1_read_data1), .in1({16{1'b0}}), .out(multiplexer_7_out), .sel(control_1_li));
  Subtractor #(.width(16)) subtractor_1 (.a(bit_extender_1_out), .b(16'h1), .out(subtractor_1_out));  // open: bin, bout
  ALU alu_1 (
    .d1(multiplexer_7_out), .d2(multiplexer_6_out), .alusignal(control_1_aluop), .bne(alu_1_bne),
    .blesignal(alu_1_blesignal), .\output (alu_1_output));
  Adder #(.width(16)) adder_2 (.a(adder_1_out), .b(subtractor_1_out), .out(adder_2_out));  // open: cin, cout
  RAM #(.addrWidth(16), .dataWidth(16), .bus("separate")) ram_1 (
    .addr(reg8_1_read_data2), .din(reg8_1_read_data1), .data(ram_1_data), .str(control_1_memwrite),
    .clk(clock), .ld(control_1_memread), .clr(reset));  // open: sel
  Multiplexer #(.width(16), .enable("false")) multiplexer_8 (
    .in0(alu_1_output), .in1(ram_1_data), .out(multiplexer_8_out), .sel(control_1_memtoreg));

  // Other names for the same wires on the sheet: WL = W; wr[2:0] = w_t

  // Notes on the sheet:
  //   contents of rom_1 (hex, n*v repeats v):
  //   d006 d00c b007 f098 d007 d208 b003 f0a0 a003 42 7000 e000
endmodule

module pipeline_add (
);

  wire alu_1_blesignal, alu_1_bne, ALUSrc, and_1_out, and_2_out, branch___jump, call, clock, clock_1_out,
       control_1_regdst, ex_mem_1_halt_2, exwrite, halt, hazard_1_flushid, hazard_1_flushif,
       hazard_1_stallid, hazard_1_stallif, memwrite, regread_1_r1read, regread_1_r2read, reset, ret, rread,
       rwrite, W;
  wire [0:0] ex_mem_1_wb_2, id_ex_1_wb_2, mem_wb_1_wb_2;
  wire [1:0] control_1_aluop, control_1_branch, control_1_memtoreg, ex_mem_1_m_2;
  wire [2:0] ex, id_ex_1_m_2_2, mem, multiplexer_4_out, readReg1, readReg1L, readReg2, w_t;
  wire [4:2] id_ex_1_m_2;
  wire [5:0] control_1_alusrc, control_1_memread;
  wire [5:1] id_ex_1_ex_2;
  wire [15:0] adder_1_out, adder_2_out, alu_1_output, bit_extender_1_out, ex_mem_1_a_2, ex_mem_1_d_2,
       ex_mem_1_output_2, id_ex_1_imm_2, id_ex_1_pc_1_2, id_ex_1_r1_2, id_ex_1_r2_2, if_id_1_instru_2,
       if_id_1_pc_1_2, jump_minus_64_1_out_2, mem_wb_1_a_2, mem_wb_1_d_2, multiplexer_1_out,
       multiplexer_2_out, multiplexer_5_out, multiplexer_6_out, multiplexer_8_out, PC_q, ra_register_1_data1,
       ram_1_data, reg8_1_read_data1, reg8_1_read_data2, rom_1_data, subtractor_1_out;

  Multiplexer #(.width(16), .enable("false")) multiplexer_1 (
    .in0(adder_1_out), .in1(adder_2_out), .out(multiplexer_1_out), .sel(branch___jump));
  Multiplexer #(.width(16), .enable("false")) multiplexer_2 (
    .in0(multiplexer_1_out), .in1(ra_register_1_data1), .out(multiplexer_2_out), .sel(rread));
  Clock clock_1 (.out(clock_1_out));
  jump_minus_64 jump_minus_64_1 (.in_1(multiplexer_2_out), .out_2(jump_minus_64_1_out_2));
  Hazard hazard_1 (
    .in_1(clock), .flushID(hazard_1_flushid), .r1read(regread_1_r1read), .r2read(regread_1_r2read), .ex(ex),
    .exwrite(exwrite), .stallIF(hazard_1_stallif), .r2(readReg2), .stallID(hazard_1_stallid), .r1(readReg1),
    .mem(mem), .memwrite(memwrite), .flushIF(hazard_1_flushif), .branch___jump(branch___jump), .w(w_t),
    .W_2(W));
  Multiplexer #(.enable("false")) multiplexer_3 (.in0(clock_1_out), .in1(1'b0), .out(clock), .sel(halt));
  Button button_1 (.out(reset));
  Register #(.width(16)) PC (.D(jump_minus_64_1_out_2), .en(hazard_1_stallif), .Q(PC_q), .clk(clock), .clr(reset));
  Adder #(.width(16)) adder_1 (.a(PC_q), .b(16'h1), .out(adder_1_out));  // open: cin, cout
  IF_ID if_id_1 (
    .PC_1(adder_1_out), .Instru(rom_1_data), .Enable(hazard_1_stallid), .PC_1_2(if_id_1_pc_1_2),
    .Instru_2({if_id_1_instru_2[15:9], readReg2, readReg1, if_id_1_instru_2[2:0]}), .clock(clock),
    .reset(hazard_1_flushif));
  ROM #(.addrWidth(16), .dataWidth(16)) rom_1 (.addr(PC_q), .data(rom_1_data));  // open: sel
  Regread regread_1 (
    .o1(if_id_1_instru_2[15]), .o2(if_id_1_instru_2[14]), .o3(if_id_1_instru_2[13]),
    .o4(if_id_1_instru_2[12]), .r1read(regread_1_r1read), .r2read(regread_1_r2read));
  Control control_1 (
    .opcode__x4_x3_x2_x1(if_id_1_instru_2[15:12]), .RegDst(control_1_regdst), .ALUSrc(control_1_alusrc[0]),
    .Memtoreg(control_1_memtoreg[0]), .RegWrite(control_1_memtoreg[1]), .MemRead(control_1_memread[0]),
    .MemWrite(control_1_memread[1]), .Branch(control_1_branch), .Jump(control_1_memread[4]),
    .ALUOp(control_1_aluop), .raread(control_1_memread[5]), .halt(control_1_alusrc[3]),
    .rawrite(control_1_alusrc[4]), .li(control_1_alusrc[5]), .call(call), .ret(ret));
  assign bit_extender_1_out = {{10{1'b0}}, {if_id_1_instru_2[11:9], if_id_1_instru_2[2:0]}};  // Bit_Extender bit_extender_1
  ra_register ra_register_1 (
    .Write(rwrite), .in_2(adder_1_out), .clock(clock), .reset(reset), .Read(rread),
    .Data1(ra_register_1_data1));
  Multiplexer #(.width(3), .enable("false")) multiplexer_4 (
    .in0(readReg1), .in1(if_id_1_instru_2[2:0]), .out(multiplexer_4_out), .sel(control_1_regdst));
  reg8 reg8_1 (
    .Write(W), .Write_register(w_t), .write_data(multiplexer_8_out), .clock(clock), .reset(reset),
    .read_register2(readReg2), .read_register1(readReg1L), .read_data1(reg8_1_read_data1),
    .read_data2(reg8_1_read_data2));
  ID_EX id_ex_1 (
    .WB(control_1_memtoreg), .M({control_1_memread[5:4], control_1_branch, control_1_memread[1:0]}),
    .EX({control_1_alusrc[5:3], control_1_aluop, control_1_alusrc[0]}), .PC_1(if_id_1_pc_1_2),
    .r1(reg8_1_read_data1), .r2(reg8_1_read_data2), .w(multiplexer_4_out), .imm(bit_extender_1_out),
    .WB_2({exwrite, id_ex_1_wb_2[0]}), .M_2({id_ex_1_m_2_2[2], id_ex_1_m_2, id_ex_1_m_2_2[1:0]}),
    .EX_2({id_ex_1_ex_2[5], rwrite, id_ex_1_ex_2[3:1], ALUSrc}), .PC_1_2(id_ex_1_pc_1_2),
    .r1_2(id_ex_1_r1_2), .r2_2(id_ex_1_r2_2), .w_2(ex), .imm_2(id_ex_1_imm_2), .clock(clock),
    .reset(hazard_1_flushid));
  and and_1 (and_1_out, id_ex_1_m_2[2], alu_1_blesignal);
  and and_2 (and_2_out, alu_1_bne, id_ex_1_m_2[3]);
  or or_1 (branch___jump, and_1_out, and_2_out, id_ex_1_m_2[4]);
  Multiplexer #(.width(16), .enable("false")) multiplexer_5 (
    .in0(id_ex_1_r2_2), .in1(id_ex_1_imm_2), .out(multiplexer_5_out), .sel(ALUSrc));
  Multiplexer #(.width(16), .enable("false")) multiplexer_6 (
    .in0(id_ex_1_r1_2), .in1({16{1'b0}}), .out(multiplexer_6_out), .sel(id_ex_1_ex_2[5]));
  Multiplexer #(.width(3), .enable("false")) multiplexer_7 (
    .in0(readReg1), .in1(readReg2), .out(readReg1L), .sel(ALUSrc));
  Subtractor #(.width(16)) subtractor_1 (.a(id_ex_1_imm_2), .b(16'h1), .out(subtractor_1_out));  // open: bin, bout
  ALU alu_1 (
    .d1(multiplexer_6_out), .d2(multiplexer_5_out), .alusignal(id_ex_1_ex_2[2:1]), .bne(alu_1_bne),
    .blesignal(alu_1_blesignal), .\output (alu_1_output));
  Adder #(.width(16)) adder_2 (.a(id_ex_1_pc_1_2), .b(subtractor_1_out), .out(adder_2_out));  // open: cin, cout
  EX_MEM ex_mem_1 (
    .WB({exwrite, id_ex_1_wb_2[0]}), .M(id_ex_1_m_2_2), .halt(id_ex_1_ex_2[3]), .A(id_ex_1_r2_2),
    .D(id_ex_1_r1_2), .w(ex), .WB_2({memwrite, ex_mem_1_wb_2[0]}), .M_2({rread, ex_mem_1_m_2}),
    .halt_2(ex_mem_1_halt_2), .A_2(ex_mem_1_a_2), .D_2(ex_mem_1_d_2), .w_2(mem), .clock(clock),
    .reset(reset), .\output (alu_1_output), .output_2(ex_mem_1_output_2));
  RAM #(.addrWidth(16), .dataWidth(16), .bus("separate")) ram_1 (
    .addr(ex_mem_1_a_2), .din(ex_mem_1_d_2), .data(ram_1_data), .str(ex_mem_1_m_2[1]), .clk(clock),
    .ld(ex_mem_1_m_2[0]), .clr(reset));  // open: sel
  MEM_WB mem_wb_1 (
    .WB({memwrite, ex_mem_1_wb_2[0]}), .halt(ex_mem_1_halt_2), .D(ram_1_data), .w(mem),
    .A(ex_mem_1_output_2), .WB_2({W, mem_wb_1_wb_2[0]}), .halt_2(halt), .D_2(mem_wb_1_d_2), .w_2(w_t),
    .A_2(mem_wb_1_a_2), .clock(clock), .reset(reset));
  Multiplexer #(.width(16), .enable("false")) multiplexer_8 (
    .in0(mem_wb_1_a_2), .in1(mem_wb_1_d_2), .out(multiplexer_8_out), .sel(mem_wb_1_wb_2[0]));

  // Other names for the same wires on the sheet: WL = W; wr[2:0] = w_t

  // Notes on the sheet:
  //   IF/ID
  //   contents of rom_1 (hex, n*v repeats v):
  //   d001 d00a d212 41 ce8f e000
  //   Hazard
  //   ID/EX
  //   Hazard
  //   EX/MEM
  //   MEM/WB
endmodule

module reg8 (
  input  Write,
  input  [2:0] Write_register,
  input  [15:0] write_data,
  input  clock,
  input  [2:0] read_register2,
  input  [2:0] read_register1,
  input  reset,
  output [15:0] read_data1,
  output [15:0] read_data2
);

  wire and_1_out, and_2_out, and_3_out, and_4_out, and_5_out, and_6_out, and_7_out, and_8_out,
       decoder_1_out0, decoder_1_out1, decoder_1_out2, decoder_1_out3, decoder_1_out4, decoder_1_out5,
       decoder_1_out6, decoder_1_out7;
  wire [15:0] register_1_q, register_2_q, register_3_q, register_4_q, register_5_q, register_6_q,
       register_7_q, register_8_q;

  Decoder #(.select(3), .enable("false")) decoder_1 (
    .out0(decoder_1_out0), .out1(decoder_1_out1), .out2(decoder_1_out2), .out3(decoder_1_out3),
    .out4(decoder_1_out4), .out5(decoder_1_out5), .out6(decoder_1_out6), .out7(decoder_1_out7),
    .sel(Write_register));
  and and_1 (and_1_out, Write, decoder_1_out0);
  and and_2 (and_2_out, Write, decoder_1_out1);
  and and_3 (and_3_out, Write, decoder_1_out2);
  and and_4 (and_4_out, Write, decoder_1_out3);
  and and_5 (and_5_out, Write, decoder_1_out4);
  and and_6 (and_6_out, Write, decoder_1_out5);
  and and_7 (and_7_out, Write, decoder_1_out6);
  and and_8 (and_8_out, Write, decoder_1_out7);
  Register #(.width(16)) register_1 (.D(write_data), .en(and_1_out), .Q(register_1_q), .clk(clock), .clr(reset));
  Register #(.width(16)) register_2 (.D(write_data), .en(and_2_out), .Q(register_2_q), .clk(clock), .clr(reset));
  Register #(.width(16)) register_3 (.D(write_data), .en(and_3_out), .Q(register_3_q), .clk(clock), .clr(reset));
  Register #(.width(16)) register_4 (.D(write_data), .en(and_4_out), .Q(register_4_q), .clk(clock), .clr(reset));
  Register #(.width(16)) register_5 (.D(write_data), .en(and_5_out), .Q(register_5_q), .clk(clock), .clr(reset));
  Register #(.width(16)) register_6 (.D(write_data), .en(and_6_out), .Q(register_6_q), .clk(clock), .clr(reset));
  Register #(.width(16)) register_7 (.D(write_data), .en(and_7_out), .Q(register_7_q), .clk(clock), .clr(reset));
  Register #(.width(16)) register_8 (.D(write_data), .en(and_8_out), .Q(register_8_q), .clk(clock), .clr(reset));
  Multiplexer #(.select(3), .width(16), .enable("false")) multiplexer_1 (
    .in0(register_1_q), .in1(register_2_q), .in2(register_3_q), .in3(register_4_q), .in4(register_5_q),
    .in5(register_6_q), .in6(register_7_q), .in7(register_8_q), .out(read_data1), .sel(read_register1));
  Multiplexer #(.select(3), .width(16), .enable("false")) multiplexer_2 (
    .in0(register_1_q), .in1(register_2_q), .in2(register_3_q), .in3(register_4_q), .in4(register_5_q),
    .in5(register_6_q), .in6(register_7_q), .in7(register_8_q), .out(read_data2), .sel(read_register2));
endmodule

module ALU (
  input  [15:0] d1,
  input  [15:0] d2,
  input  [1:0] alusignal,
  output bne,
  output blesignal,
  output [15:0] \output 
);

  wire comparator_1_eq, comparator_1_lt;
  wire [15:0] adder_1_out, and_1_out, or_1_out;

  Comparator #(.width(16), .mode("unsigned")) comparator_1 (
    .a(d1), .b(d2), .eq(comparator_1_eq), .lt(comparator_1_lt));  // open: gt
  Adder #(.width(16)) adder_1 (.a(d1), .b(d2), .out(adder_1_out));  // open: cin, cout
  assign and_1_out = d1 & d2;  // AND_Gate and_1, 16 bits wide
  assign or_1_out = d1 | d2;  // OR_Gate or_1, 16 bits wide
  not not_1 (bne, comparator_1_eq);
  or or_2 (blesignal, comparator_1_eq, comparator_1_lt);
  Multiplexer #(.select(2), .width(16)) multiplexer_1 (
    .in1(adder_1_out), .in2(and_1_out), .in3(or_1_out), .out(\output ), .sel(alusignal), .en(1'b1));  // open: in0
endmodule

module Mycontrol (
  input  x4,
  input  x3,
  input  x2,
  input  x1,
  output RegDst,
  output ALUSrc,
  output memtoreg,
  output RegWrite,
  output MemRead,
  output MemWrite,
  output [1:0] Branch,
  output Jump,
  output ALU01,
  output ALU02,
  output raread,
  output rawrite,
  output halt,
  output li,
  output call,
  output ret
);

  wire and_1_out, and_2_out, and_3_out, and_4_out, and_5_out, and_6_out, and_8_out, and_9_out, and_10_out,
       and_11_out, and_12_out, and_17_out, and_18_out, and_19_out, and_20_out, and_21_out, and_22_out,
       and_23_out, and_24_out, and_25_out, and_26_out, not_1_out, not_2_out, not_3_out, not_4_out, not_5_out,
       not_6_out, not_7_out, not_8_out, not_9_out, not_10_out, not_11_out, not_12_out, not_13_out,
       not_14_out, not_15_out, not_16_out, not_17_out, not_18_out, not_19_out, not_20_out, not_21_out,
       not_22_out, not_23_out, not_24_out, not_25_out, not_26_out, not_27_out, not_28_out, not_29_out,
       not_30_out, not_31_out, not_32_out, not_33_out, not_34_out, not_35_out, not_36_out, not_37_out,
       not_38_out, not_39_out, not_40_out, not_41_out, not_42_out, not_43_out, not_44_out, not_45_out,
       not_46_out, not_47_out, not_48_out, not_49_out, not_50_out, not_51_out, not_52_out, not_53_out,
       not_54_out, not_55_out, not_56_out, not_57_out, or_1_out;

  not not_1 (not_1_out, x4);
  not not_2 (not_2_out, x3);
  not not_3 (not_3_out, x2);
  not not_4 (not_4_out, x1);
  not not_5 (not_5_out, x4);
  not not_6 (not_6_out, x2);
  not not_7 (not_7_out, x4);
  not not_8 (not_8_out, x1);
  not not_9 (not_9_out, x4);
  not not_10 (not_10_out, x3);
  or or_1 (or_1_out, x2, x1);
  not not_11 (not_11_out, x3);
  not not_12 (not_12_out, x2);
  not not_13 (not_13_out, x1);
  not not_14 (not_14_out, x3);
  not not_15 (not_15_out, x2);
  not not_16 (not_16_out, x1);
  not not_17 (not_17_out, x4);
  not not_18 (not_18_out, x3);
  not not_19 (not_19_out, x4);
  not not_20 (not_20_out, x1);
  not not_21 (not_21_out, x2);
  not not_22 (not_22_out, x3);
  not not_23 (not_23_out, x2);
  not not_24 (not_24_out, x1);
  not not_25 (not_25_out, x3);
  not not_26 (not_26_out, x2);
  not not_27 (not_27_out, x1);
  not not_28 (not_28_out, x3);
  not not_29 (not_29_out, x2);
  not not_30 (not_30_out, x2);
  not not_31 (not_31_out, x1);
  not not_32 (not_32_out, x4);
  not not_33 (not_33_out, x2);
  not not_34 (not_34_out, x1);
  not not_35 (not_35_out, x4);
  not not_36 (not_36_out, x3);
  not not_37 (not_37_out, x4);
  not not_38 (not_38_out, x2);
  not not_39 (not_39_out, x4);
  not not_40 (not_40_out, x3);
  not not_41 (not_41_out, x4);
  not not_42 (not_42_out, x1);
  not not_43 (not_43_out, x4);
  not not_44 (not_44_out, x3);
  not not_45 (not_45_out, x2);
  not not_46 (not_46_out, x4);
  not not_47 (not_47_out, x3);
  not not_48 (not_48_out, x4);
  not not_49 (not_49_out, x1);
  not not_50 (not_50_out, x3);
  not not_51 (not_51_out, x2);
  not not_52 (not_52_out, x4);
  not not_53 (not_53_out, x3);
  not not_54 (not_54_out, x1);
  not not_55 (not_55_out, x2);
  not not_56 (not_56_out, x3);
  not not_57 (not_57_out, x4);
  and and_1 (and_1_out, not_1_out, not_2_out, not_3_out, not_4_out);
  and and_2 (and_2_out, not_5_out, x3, not_6_out, x1);
  and and_3 (and_3_out, not_7_out, x3, x2, not_8_out);
  and and_4 (and_4_out, not_9_out, not_10_out, or_1_out);
  and and_5 (and_5_out, x4, x3, x1);
  and and_6 (and_6_out, x4, not_11_out, not_12_out, not_13_out);
  and and_7 (memtoreg, x4, not_14_out, not_15_out, not_16_out);
  and and_8 (and_8_out, not_17_out, not_18_out);
  and and_9 (and_9_out, not_19_out, x2, not_20_out);
  and and_10 (and_10_out, x3, not_21_out, x1);
  and and_11 (and_11_out, x4, x3, x1);
  and and_12 (and_12_out, not_22_out, not_23_out, not_24_out);
  and and_13 (MemRead, x4, not_25_out, not_26_out, not_27_out);
  and and_14 (MemWrite, x4, not_28_out, not_29_out, x1);
  and and_15 (Branch[0], x4, x3, not_30_out, not_31_out);
  and and_16 (Branch[1], not_32_out, x3, not_33_out, not_34_out);
  and and_17 (and_17_out, not_35_out, x3, x2, x1);
  and and_18 (and_18_out, x4, not_36_out, x2);
  and and_19 (and_19_out, not_37_out, x3, not_38_out, x1);
  and and_20 (and_20_out, not_39_out, not_40_out, x2);
  and and_21 (and_21_out, not_41_out, x2, not_42_out);
  and and_22 (and_22_out, not_43_out, not_44_out, not_45_out);
  and and_23 (and_23_out, not_46_out, not_47_out, x1);
  and and_24 (and_24_out, not_48_out, x3, x2, not_49_out);
  and and_25 (and_25_out, x4, x3, x1);
  and and_26 (and_26_out, x4, not_50_out, not_51_out);
  and and_27 (raread, not_52_out, x3, x2, x1);
  and and_28 (rawrite, x4, not_53_out, x2, x1);
  and and_29 (halt, x4, x3, x2, not_54_out);
  and and_30 (li, x4, x3, not_55_out, x1);
  and and_31 (call, x4, not_56_out, x2, x1);
  and and_32 (ret, not_57_out, x3, x2, x1);
  or or_2 (RegDst, and_1_out, and_2_out, and_3_out);
  or or_3 (ALUSrc, and_4_out, and_5_out, and_6_out);
  or or_4 (RegWrite, and_8_out, and_9_out, and_10_out, and_11_out, and_12_out);
  or or_5 (Jump, and_17_out, and_18_out);
  or or_6 (ALU01, and_19_out, and_20_out, and_21_out);
  or or_7 (ALU02, and_22_out, and_23_out, and_24_out, and_25_out, and_26_out);

  // Notes on the sheet:
  //   read from bottom to top
endmodule

module Control (
  input  [3:0] opcode__x4_x3_x2_x1,
  output RegDst,
  output ALUSrc,
  output Memtoreg,
  output RegWrite,
  output MemRead,
  output MemWrite,
  output [1:0] Branch,
  output Jump,
  output [1:0] ALUOp,
  output raread,
  output halt,
  output rawrite,
  output li,
  output call,
  output ret
);

  Mycontrol mycontrol_1 (
    .x4(opcode__x4_x3_x2_x1[3]), .x3(opcode__x4_x3_x2_x1[2]), .x2(opcode__x4_x3_x2_x1[1]),
    .x1(opcode__x4_x3_x2_x1[0]), .RegDst(RegDst), .ALUSrc(ALUSrc), .memtoreg(Memtoreg), .RegWrite(RegWrite),
    .MemRead(MemRead), .MemWrite(MemWrite), .Branch(Branch), .Jump(Jump), .ALU01(ALUOp[1]), .ALU02(ALUOp[0]),
    .raread(raread), .rawrite(rawrite), .halt(halt), .li(li), .call(call), .ret(ret));
endmodule

module ra_register (
  input  Write,
  input  [15:0] in_2,
  input  Read,
  input  clock,
  input  reset,
  output [15:0] Data1
);

  wire [15:0] register_1_q;

  assign Data1 = Read ? register_1_q : 16'bz;  // Controlled_Buffer controlled_buffer_1
  Register #(.width(16)) register_1 (.D(in_2), .en(Write), .Q(register_1_q), .clk(clock), .clr(reset));
endmodule

module jump_minus_64 (
  input  [15:0] in_1,
  output [15:0] out_2
);

  wire comparator_1_gt;
  wire [15:0] subtractor_1_out;

  Subtractor #(.width(16)) subtractor_1 (.a(in_1), .b(16'h40), .out(subtractor_1_out));  // open: bin, bout
  Comparator #(.width(16), .mode("unsigned")) comparator_1 (
    .a(in_1), .b(16'h40), .gt(comparator_1_gt));  // open: eq, lt
  Multiplexer #(.width(16), .enable("false")) multiplexer_1 (
    .in0(in_1), .in1(subtractor_1_out), .out(out_2), .sel(comparator_1_gt));
endmodule

module controlAnalyze (
  input  x4,
  input  x3,
  input  x2,
  input  x1,
  output RegDst,
  output ALUSrc,
  output memtoreg,
  output RegWrite,
  output MemRead,
  output MemWrite,
  output Branch,
  output Jump,
  output ALU01,
  output ALU02
);

  wire and_1_out, and_2_out, and_3_out, and_4_out, and_5_out, and_6_out, and_8_out, and_9_out, and_10_out,
       and_11_out, and_12_out, and_16_out, and_17_out, and_18_out, and_19_out, and_20_out, and_21_out,
       and_22_out, and_23_out, and_24_out, and_25_out, not_1_out, not_2_out, not_3_out, not_4_out, not_5_out,
       not_6_out, not_7_out, not_8_out, not_9_out, not_10_out, not_11_out, not_12_out, not_13_out,
       not_14_out, not_15_out, not_16_out, not_17_out, not_18_out, not_19_out, not_20_out, not_21_out,
       not_22_out, not_23_out, not_24_out, not_25_out, not_26_out, not_27_out, not_28_out, not_29_out,
       not_30_out, not_31_out, not_32_out, not_33_out, not_34_out, not_35_out, not_36_out, not_37_out,
       not_38_out, not_39_out, not_40_out, not_41_out, not_42_out, not_43_out, not_44_out, not_45_out,
       not_46_out, not_47_out, or_1_out;

  not not_1 (not_1_out, x4);
  not not_2 (not_2_out, x3);
  not not_3 (not_3_out, x2);
  not not_4 (not_4_out, x1);
  not not_5 (not_5_out, x4);
  not not_6 (not_6_out, x2);
  not not_7 (not_7_out, x4);
  not not_8 (not_8_out, x1);
  not not_9 (not_9_out, x4);
  not not_10 (not_10_out, x3);
  or or_1 (or_1_out, x2, x1);
  not not_11 (not_11_out, x3);
  not not_12 (not_12_out, x2);
  not not_13 (not_13_out, x3);
  not not_14 (not_14_out, x2);
  not not_15 (not_15_out, x1);
  not not_16 (not_16_out, x4);
  not not_17 (not_17_out, x3);
  not not_18 (not_18_out, x4);
  not not_19 (not_19_out, x1);
  not not_20 (not_20_out, x2);
  not not_21 (not_21_out, x3);
  not not_22 (not_22_out, x2);
  not not_23 (not_23_out, x1);
  not not_24 (not_24_out, x3);
  not not_25 (not_25_out, x2);
  not not_26 (not_26_out, x1);
  not not_27 (not_27_out, x3);
  not not_28 (not_28_out, x2);
  not not_29 (not_29_out, x2);
  not not_30 (not_30_out, x1);
  not not_31 (not_31_out, x4);
  not not_32 (not_32_out, x3);
  not not_33 (not_33_out, x4);
  not not_34 (not_34_out, x2);
  not not_35 (not_35_out, x4);
  not not_36 (not_36_out, x3);
  not not_37 (not_37_out, x4);
  not not_38 (not_38_out, x1);
  not not_39 (not_39_out, x4);
  not not_40 (not_40_out, x3);
  not not_41 (not_41_out, x2);
  not not_42 (not_42_out, x4);
  not not_43 (not_43_out, x3);
  not not_44 (not_44_out, x4);
  not not_45 (not_45_out, x1);
  not not_46 (not_46_out, x3);
  not not_47 (not_47_out, x2);
  and and_1 (and_1_out, not_1_out, not_2_out, not_3_out, not_4_out);
  and and_2 (and_2_out, not_5_out, x3, not_6_out, x1);
  and and_3 (and_3_out, not_7_out, x3, x2, not_8_out);
  and and_4 (and_4_out, not_9_out, not_10_out, or_1_out);
  and and_5 (and_5_out, x4, x3, x1);
  and and_6 (and_6_out, x4, not_11_out, not_12_out);
  and and_7 (memtoreg, x4, not_13_out, not_14_out, not_15_out);
  and and_8 (and_8_out, not_16_out, not_17_out);
  and and_9 (and_9_out, not_18_out, x2, not_19_out);
  and and_10 (and_10_out, x3, not_20_out, x1);
  and and_11 (and_11_out, x4, x3, x1);
  and and_12 (and_12_out, not_21_out, not_22_out, not_23_out);
  and and_13 (MemRead, x4, not_24_out, not_25_out, not_26_out);
  and and_14 (MemWrite, x4, not_27_out, not_28_out, x1);
  and and_15 (Branch, x3, not_29_out, not_30_out);
  and and_16 (and_16_out, not_31_out, x3, x2, x1);
  and and_17 (and_17_out, x4, not_32_out, x2);
  and and_18 (and_18_out, not_33_out, x3, not_34_out, x1);
  and and_19 (and_19_out, not_35_out, not_36_out, x2);
  and and_20 (and_20_out, not_37_out, x2, not_38_out);
  and and_21 (and_21_out, not_39_out, not_40_out, not_41_out);
  and and_22 (and_22_out, not_42_out, not_43_out, x1);
  and and_23 (and_23_out, not_44_out, x3, x2, not_45_out);
  and and_24 (and_24_out, x4, x3, x1);
  and and_25 (and_25_out, x4, not_46_out, not_47_out);
  or or_2 (RegDst, and_1_out, and_2_out, and_3_out);
  or or_3 (ALUSrc, and_4_out, and_5_out, and_6_out);
  or or_4 (RegWrite, and_8_out, and_9_out, and_10_out, and_11_out, and_12_out);
  or or_5 (Jump, and_16_out, and_17_out);
  or or_6 (ALU01, and_18_out, and_19_out, and_20_out);
  or or_7 (ALU02, and_21_out, and_22_out, and_23_out, and_24_out, and_25_out);

  // Notes on the sheet:
  //   read from bottom to top
endmodule

module IF_ID (
  input  [15:0] PC_1,
  input  [15:0] Instru,
  input  Enable,
  input  clock,
  input  reset,
  output [15:0] PC_1_2,
  output [15:0] Instru_2
);

  Register #(.width(16)) register_1 (.D(PC_1), .en(Enable), .Q(PC_1_2), .clk(clock), .clr(reset));
  Register #(.width(16)) register_2 (.D(Instru), .en(Enable), .Q(Instru_2), .clk(clock), .clr(reset));
endmodule

module ID_EX (
  input  [1:0] WB,
  input  [5:0] M,
  input  [5:0] EX,
  input  [15:0] PC_1,
  input  [15:0] r1,
  input  [15:0] r2,
  input  [2:0] w,
  input  [15:0] imm,
  input  clock,
  input  reset,
  output [1:0] WB_2,
  output [5:0] M_2,
  output [5:0] EX_2,
  output [15:0] PC_1_2,
  output [15:0] r1_2,
  output [15:0] r2_2,
  output [2:0] w_2,
  output [15:0] imm_2
);

  Register #(.width(2)) register_1 (.D(WB), .en(1'b1), .Q(WB_2), .clk(clock), .clr(reset));
  Register #(.width(6)) register_2 (.D(M), .en(1'b1), .Q(M_2), .clk(clock), .clr(reset));
  Register #(.width(6)) register_3 (.D(EX), .en(1'b1), .Q(EX_2), .clk(clock), .clr(reset));
  Register #(.width(16)) register_4 (.D(PC_1), .en(1'b1), .Q(PC_1_2), .clk(clock), .clr(reset));
  Register #(.width(16)) register_5 (.D(r1), .en(1'b1), .Q(r1_2), .clk(clock), .clr(reset));
  Register #(.width(16)) register_6 (.D(r2), .en(1'b1), .Q(r2_2), .clk(clock), .clr(reset));
  Register #(.width(3)) register_7 (.D(w), .en(1'b1), .Q(w_2), .clk(clock), .clr(reset));
  Register #(.width(16)) register_8 (.D(imm), .en(1'b1), .Q(imm_2), .clk(clock), .clr(reset));
endmodule

module EX_MEM (
  input  [1:0] WB,
  input  [2:0] M,
  input  halt,
  input  [15:0] \output ,
  input  [15:0] A,
  input  [15:0] D,
  input  [2:0] w,
  input  clock,
  input  reset,
  output [1:0] WB_2,
  output [2:0] M_2,
  output halt_2,
  output [15:0] output_2,
  output [15:0] A_2,
  output [15:0] D_2,
  output [2:0] w_2
);

  Register #(.width(2)) register_1 (.D(WB), .en(1'b1), .Q(WB_2), .clk(clock), .clr(reset));
  Register #(.width(3)) register_2 (.D(M), .en(1'b1), .Q(M_2), .clk(clock), .clr(reset));
  Register #(.width(1)) register_3 (.D(halt), .en(1'b1), .Q(halt_2), .clk(clock), .clr(reset));
  Register #(.width(16)) register_4 (.D(\output ), .en(1'b1), .Q(output_2), .clk(clock), .clr(reset));
  Register #(.width(16)) register_5 (.D(A), .en(1'b1), .Q(A_2), .clk(clock), .clr(reset));
  Register #(.width(16)) register_6 (.D(D), .en(1'b1), .Q(D_2), .clk(clock), .clr(reset));
  Register #(.width(3)) register_7 (.D(w), .en(1'b1), .Q(w_2), .clk(clock), .clr(reset));
endmodule

module MEM_WB (
  input  [1:0] WB,
  input  halt,
  input  [15:0] D,
  input  [2:0] w,
  input  [15:0] A,
  input  clock,
  input  reset,
  output [1:0] WB_2,
  output halt_2,
  output [15:0] D_2,
  output [2:0] w_2,
  output [15:0] A_2
);

  Register #(.width(2)) register_1 (.D(WB), .en(1'b1), .Q(WB_2), .clk(clock), .clr(reset));
  Register #(.width(1)) register_2 (.D(halt), .en(1'b1), .Q(halt_2), .clk(clock), .clr(reset));
  Register #(.width(16)) register_3 (.D(D), .en(1'b1), .Q(D_2), .clk(clock), .clr(reset));
  Register #(.width(3)) register_4 (.D(w), .en(1'b1), .Q(w_2), .clk(clock), .clr(reset));
  Register #(.width(16)) register_5 (.D(A), .en(1'b1), .Q(A_2), .clk(clock), .clr(reset));
endmodule

module Regread (
  input  o1,
  input  o2,
  input  o3,
  input  o4,
  output r1read,
  output r2read
);

  wire and_1_out, and_2_out, and_3_out, and_4_out, and_5_out, and_6_out, and_7_out, and_8_out, and_9_out,
       and_10_out, and_11_out, not_1_out, not_2_out, not_3_out, not_4_out, not_5_out, not_6_out, not_7_out,
       not_8_out, not_9_out, not_10_out, not_11_out, not_12_out, not_13_out, not_14_out, not_15_out,
       not_16_out, not_17_out, not_18_out, not_19_out;

  not not_1 (not_1_out, o1);
  not not_2 (not_2_out, o2);
  not not_3 (not_3_out, o1);
  not not_4 (not_4_out, o3);
  not not_5 (not_5_out, o1);
  not not_6 (not_6_out, o4);
  not not_7 (not_7_out, o2);
  not not_8 (not_8_out, o3);
  not not_9 (not_9_out, o3);
  not not_10 (not_10_out, o4);
  not not_11 (not_11_out, o3);
  not not_12 (not_12_out, o3);
  not not_13 (not_13_out, o3);
  not not_14 (not_14_out, o1);
  not not_15 (not_15_out, o2);
  not not_16 (not_16_out, o1);
  not not_17 (not_17_out, o4);
  not not_18 (not_18_out, o3);
  not not_19 (not_19_out, o3);
  and and_1 (and_1_out, not_1_out, not_2_out);
  and and_2 (and_2_out, not_3_out, not_4_out);
  and and_3 (and_3_out, not_5_out, not_6_out);
  and and_4 (and_4_out, not_7_out, not_8_out);
  and and_5 (and_5_out, not_9_out, not_10_out);
  and and_6 (and_6_out, o1, o2, o3, o4);
  and and_7 (and_7_out, not_14_out, not_15_out, o4);
  and and_8 (and_8_out, not_16_out, o3, not_17_out);
  and and_9 (and_9_out, o2, not_18_out);
  and and_10 (and_10_out, o1, not_19_out);
  and and_11 (and_11_out, o1, o2, o4);
  or or_1 (r1read, and_1_out, and_2_out, and_3_out, and_4_out, and_5_out, and_6_out);
  or or_2 (r2read, not_11_out, not_12_out, not_13_out, and_7_out, and_8_out, and_9_out, and_10_out, and_11_out);
endmodule

module Hazard (
  input  in_1,
  input  r1read,
  input  r2read,
  input  [2:0] ex,
  input  exwrite,
  input  [2:0] r2,
  input  [2:0] r1,
  input  [2:0] mem,
  input  memwrite,
  input  branch___jump,
  input  [2:0] w,
  input  W_2,
  output flushID,
  output stallIF,
  output stallID,
  output flushIF
);

  wire and_1_out, and_2_out, and_3_out, and_4_out, and_5_out, and_6_out, and_7_out, and_8_out, and_9_out,
       comparator_1_eq, comparator_2_eq, comparator_3_eq, comparator_4_eq, comparator_5_eq, comparator_6_eq,
       d_ff_1_q, d_ff_2_q, or_1_out, or_2_out, or_3_out, or_4_out;

  Comparator #(.width(3)) comparator_1 (.a(ex), .b(r2), .eq(comparator_1_eq));  // open: gt, lt
  Comparator #(.width(3)) comparator_2 (.a(ex), .b(r1), .eq(comparator_2_eq));  // open: gt, lt
  Comparator #(.width(3)) comparator_3 (.a(mem), .b(r2), .eq(comparator_3_eq));  // open: gt, lt
  Comparator #(.width(3)) comparator_4 (.a(mem), .b(r1), .eq(comparator_4_eq));  // open: gt, lt
  Comparator #(.width(3)) comparator_5 (.a(w), .b(r2), .eq(comparator_5_eq));  // open: gt, lt
  Comparator #(.width(3)) comparator_6 (.a(w), .b(r1), .eq(comparator_6_eq));  // open: gt, lt
  and and_1 (and_1_out, comparator_1_eq, r2read);
  and and_2 (and_2_out, comparator_2_eq, r1read);
  and and_3 (and_3_out, comparator_3_eq, r2read);
  and and_4 (and_4_out, comparator_4_eq, r1read);
  and and_5 (and_5_out, comparator_5_eq, r2read);
  and and_6 (and_6_out, comparator_6_eq, r1read);
  or or_1 (or_1_out, and_1_out, and_2_out);
  or or_2 (or_2_out, and_3_out, and_4_out);
  or or_3 (or_3_out, and_5_out, and_6_out);
  and and_7 (and_7_out, exwrite, or_1_out);
  or or_4 (or_4_out, and_7_out, and_8_out, and_9_out);
  and and_8 (and_8_out, memwrite, or_2_out);
  and and_9 (and_9_out, W_2, or_3_out);
  D_Flip_Flop #(.trigger("falling")) d_ff_1 (.clk(in_1), .D(or_4_out), .Q(d_ff_1_q));  // open: Qn, preset, en, reset
  not not_1 (stallIF, or_4_out);
  not not_2 (stallID, or_4_out);
  and and_10 (flushID, in_1, d_ff_1_q);
  D_Flip_Flop #(.trigger("falling")) d_ff_2 (
    .clk(in_1), .D(branch___jump), .Q(d_ff_2_q));  // open: Qn, preset, en, reset
  and and_11 (flushIF, ~in_1, d_ff_2_q);  // AND_Gate

  // Other names for the same wires on the sheet: clock = in_1
endmodule
